// Logisim project lamija_ahmetasevic_22109.circ as structural Verilog: 10 circuits, main circuit main
module main (
  input  clear,
  input  reset
);

  wire clocc_out, incrementer_1_p2, incrementer_3_p2, incrementer_4_p1, jr_1_izlaz, mainctrl_1_beq,
       mainctrl_1_bne, mainctrl_1_ext, mainctrl_1_j, mainctrl_1_jal, mainctrl_1_load, mainctrl_1_memtoreg,
       mainctrl_1_rw, mainctrl_1_store, nextpc_1_pcsrc, or_1_out, zero_1_out_2;
  wire [3:0] functoalu_1_alu, multiplexer_8_out, optoalu_1_alu;
  wire [4:0] multiplexer_3_out, multiplexer_4_out;
  wire [29:0] incrementer_2_p3, nextpc_1_adress;
  wire [31:0] ext_1_izlaz, incrementer_5_p1, mips_alu_1_p5, mips_ram_1_p7, mipsprogramrom_1_p1,
       multiplexer_1_out, multiplexer_5_out, multiplexer_6_out, multiplexer_7_out, register_1_q,
       registerfile_1_p7, registerfile_1_p8;
  wire [31:2] multiplexer_2_out;

  Multiplexer #(.width(32), .enable("false")) multiplexer_1 (
    .in0({multiplexer_2_out, 2'b00}), .in1(registerfile_1_p7), .out(multiplexer_1_out), .sel(jr_1_izlaz));
  Multiplexer #(.width(30), .enable("false")) multiplexer_2 (
    .in0(incrementer_2_p3), .in1(nextpc_1_adress), .out(multiplexer_2_out), .sel(nextpc_1_pcsrc));
  Clock clocc (.out(clocc_out));
  Register #(.width(32), .trigger("falling")) register_1 (
    .D(multiplexer_1_out), .en(1'b1), .clk(clocc_out), .Q(register_1_q), .clr(reset));
  jr jr_1 (.func(mipsprogramrom_1_p1[5:0]), .OpCode(mipsprogramrom_1_p1[31:26]), .izlaz(jr_1_izlaz));
  // Incrementer #(.width(32)) incrementer_1: pin names not known; wires that end beside it: register_1_q, incrementer_1_p2
  // Incrementer #(.width(30)) incrementer_2: pin names not known; wires that end beside it: register_1_q, register_1_q[31:2], incrementer_2_p3
  // Incrementer #(.width(32)) incrementer_3: pin names not known; wires that end beside it: incrementer_1_p2, incrementer_3_p2, incrementer_3_p2
  // MIPSProgramROM mipsprogramrom_1: pin names not known; wires that end beside it: mipsprogramrom_1_p1
  // Incrementer #(.width(32)) incrementer_4: pin names not known; wires that end beside it: incrementer_4_p1, incrementer_4_p1
  // Incrementer #(.width(32)) incrementer_5: pin names not known; wires that end beside it: incrementer_5_p1
  Ext ext_1 (.Imm(mipsprogramrom_1_p1[15:0]), .ext(mainctrl_1_ext), .izlaz(ext_1_izlaz));
  mainCtrl mainctrl_1 (
    .in_1(mipsprogramrom_1_p1[31:26]), .RW(mainctrl_1_rw), .MemToReg(mainctrl_1_memtoreg),
    .Store(mainctrl_1_store), .Load(mainctrl_1_load), .ext(mainctrl_1_ext), .beq(mainctrl_1_beq),
    .bne(mainctrl_1_bne), .j(mainctrl_1_j), .jal(mainctrl_1_jal));
  or or_1 (or_1_out, mipsprogramrom_1_p1[29], mipsprogramrom_1_p1[26], mipsprogramrom_1_p1[27], mipsprogramrom_1_p1[28], mipsprogramrom_1_p1[30], mipsprogramrom_1_p1[31]);
  Multiplexer #(.width(5), .enable("false")) multiplexer_3 (
    .in0(mipsprogramrom_1_p1[15:11]), .in1(mipsprogramrom_1_p1[20:16]), .out(multiplexer_3_out),
    .sel(or_1_out));
  Multiplexer #(.width(5), .enable("false")) multiplexer_4 (
    .in0(multiplexer_3_out), .in1({5{1'b1}}), .out(multiplexer_4_out), .sel(mainctrl_1_jal));
  Multiplexer #(.width(32), .enable("false")) multiplexer_5 (
    .in0(multiplexer_6_out), .in1(incrementer_5_p1), .out(multiplexer_5_out), .sel(mainctrl_1_jal));
  // RegisterFile registerfile_1: pin names not known; wires that end beside it: multiplexer_5_out, clocc_out, mainctrl_1_rw, multiplexer_4_out, mipsprogramrom_1_p1[25:21], mipsprogramrom_1_p1[20:16], registerfile_1_p7, registerfile_1_p8
  FuncToALU functoalu_1 (.Func(mipsprogramrom_1_p1[5:0]), .ALU(functoalu_1_alu));
  OPtoALU optoalu_1 (.OpCode(mipsprogramrom_1_p1[31:26]), .ALU(optoalu_1_alu));
  Multiplexer #(.width(32), .enable("false")) multiplexer_6 (
    .in0(mips_alu_1_p5), .in1(mips_ram_1_p7), .out(multiplexer_6_out), .sel(mainctrl_1_memtoreg));
  Multiplexer #(.width(32), .enable("false")) multiplexer_7 (
    .in0(registerfile_1_p8), .in1(ext_1_izlaz), .out(multiplexer_7_out), .sel(or_1_out));
  Multiplexer #(.width(4), .enable("false")) multiplexer_8 (
    .in0(functoalu_1_alu), .in1(optoalu_1_alu), .out(multiplexer_8_out), .sel(or_1_out));
  // Mips_ALU mips_alu_1: pin names not known; wires that end beside it: registerfile_1_p7, multiplexer_7_out, multiplexer_8_out, mipsprogramrom_1_p1[10:6], mips_alu_1_p5
  // MIPS_RAM #(.addrWidth(24)) mips_ram_1: pin names not known; wires that end beside it: mips_alu_1_p5[23:0], registerfile_1_p8, mainctrl_1_store, clocc_out, mainctrl_1_load, clear, mips_ram_1_p7
  Zero zero_1 (.in_1(mips_alu_1_p5), .out_2(zero_1_out_2));
  NextPC nextpc_1 (
    .IntPC(incrementer_2_p3), .Imm26(mipsprogramrom_1_p1[25:0]), .zero(zero_1_out_2), .bne(mainctrl_1_bne),
    .beq(mainctrl_1_beq), .JaL(mainctrl_1_jal), .J(mainctrl_1_j), .Adress(nextpc_1_adress),
    .PCsrc(nextpc_1_pcsrc));

  // Notes on the sheet:
  //   contents of mipsprogramrom_1 (hex, n*v repeats v):
  //   funkcija: subu $2, $4, $5 jr $31  main: addiu $8, $0, 4 ori $9, $0, 0xabcd sll $9, $9, 16 ori $9,
  //   $9, 0x1234 sw $9, 0($8) sw $9, 4($8) ori $10, $0, 4 addu $12, $8, $10 lw $13, 0($12) addu $5, $0,
  //   $13 addiu $4, $5, 8 jal funkcija sw $2, 8($8)
endmodule

module Jump (
  input  in_1,
  input  in_2,
  input  in_3,
  input  in_4,
  input  in_5,
  input  in_6,
  output j
);

  wire not_1_out, not_2_out, not_3_out, not_4_out, not_5_out;

  not not_1 (not_1_out, in_1);
  not not_2 (not_2_out, in_2);
  not not_3 (not_3_out, in_4);
  not not_4 (not_4_out, in_5);
  not not_5 (not_5_out, in_6);
  and and_1 (j, not_1_out, not_2_out, in_3, not_3_out, not_4_out, not_5_out);
endmodule

module JaL (
  input  [5:0] opCode,
  output i
);

  wire not_1_out, not_2_out, not_3_out, not_4_out;

  not not_1 (not_1_out, opCode[2]);
  not not_2 (not_2_out, opCode[3]);
  not not_3 (not_3_out, opCode[4]);
  not not_4 (not_4_out, opCode[5]);
  and and_1 (i, opCode[0], opCode[1], not_1_out, not_2_out, not_3_out, not_4_out);
endmodule

module FuncToALU (
  input  [5:0] Func,
  output [3:0] ALU
);

  wire and_1_out, and_2_out;

  and and_1 (and_1_out, Func[5], ~Func[2]);  // AND_Gate
  or or_1 (ALU[1], and_1_out, and_2_out);
  and and_2 (and_2_out, Func[5], Func[0]);
  and and_3 (ALU[0], ~Func[5], Func[0]);  // AND_Gate

  assign ALU[3:2] = Func[2:1];
endmodule

module OPtoALU (
  input  [5:0] OpCode,
  output [3:0] ALU
);

  wire and_2_out, and_3_out;

  and and_1 (ALU[3], OpCode[3], OpCode[2]);
  and and_2 (and_2_out, ~OpCode[3], ~OpCode[1]);  // AND_Gate
  and and_3 (and_3_out, OpCode[1], ~OpCode[0]);  // AND_Gate
  or or_1 (ALU[1], ~OpCode[3], OpCode[0]);  // OR_Gate
  or or_2 (ALU[2], and_2_out, and_3_out);

  assign ALU[0] = 1'b0;
endmodule

module mainCtrl (
  input  [5:0] in_1,
  output RW,
  output MemToReg,
  output Store,
  output Load,
  output ext,
  output beq,
  output bne,
  output j,
  output jal
);

  wire and_1_out, and_2_out, and_3_out, not_1_out, not_2_out, not_3_out, not_4_out, not_5_out, not_6_out,
       not_7_out, not_8_out, not_9_out, not_10_out, not_11_out, not_12_out, not_13_out;

  not not_1 (not_1_out, in_1[2]);
  not not_2 (not_2_out, in_1[2]);
  not not_3 (not_3_out, in_1[1]);
  not not_4 (not_4_out, in_1[3]);
  not not_5 (not_5_out, in_1[5]);
  not not_6 (not_6_out, in_1[3]);
  and and_1 (and_1_out, not_2_out, not_3_out);
  and and_2 (and_2_out, not_4_out, not_1_out, in_1[0]);
  and and_3 (and_3_out, not_5_out, in_1[3]);
  not not_7 (not_7_out, in_1[3]);
  not not_8 (not_8_out, in_1[0]);
  not not_9 (not_9_out, in_1[3]);
  not not_10 (not_10_out, in_1[1]);
  not not_11 (not_11_out, in_1[3]);
  not not_12 (not_12_out, in_1[0]);
  not not_13 (not_13_out, in_1[5]);
  and and_4 (Store, in_1[5], in_1[3]);
  and and_5 (Load, in_1[5], not_6_out);
  and and_6 (beq, not_7_out, in_1[2], not_8_out);
  and and_7 (bne, not_9_out, not_10_out, in_1[0]);
  and and_8 (j, not_11_out, in_1[1], not_12_out);
  and and_9 (jal, not_13_out, in_1[1], in_1[0]);
  or or_1 (RW, and_1_out, and_2_out, and_3_out);
  not not_14 (ext, in_1[2]);

  assign MemToReg = in_1[5];
endmodule

module NextPC (
  input  [29:0] IntPC,
  input  [25:0] Imm26,
  input  zero,
  input  bne,
  input  beq,
  input  JaL,
  input  J,
  output [29:0] Adress,
  output PCsrc
);

  wire and_1_out, and_2_out, or_2_out;
  wire [29:0] adder_1_out, bit_extender_1_out;

  assign bit_extender_1_out = {{14{Imm26[15]}}, Imm26[15:0]};  // Bit_Extender bit_extender_1
  Adder #(.width(30)) adder_1 (.a(IntPC), .b(bit_extender_1_out), .out(adder_1_out));  // open: cin, cout
  Multiplexer #(.width(30), .enable("false")) multiplexer_1 (
    .in0(adder_1_out), .in1({IntPC[29:26], Imm26}), .out(Adress), .sel(or_2_out));
  or or_1 (PCsrc, and_1_out, or_2_out, and_2_out);
  and and_1 (and_1_out, ~zero, bne);  // AND_Gate
  or or_2 (or_2_out, JaL, J);
  and and_2 (and_2_out, zero, beq);
endmodule

module Zero (
  input  [31:0] in_1,
  output out_2
);

  nor nor_1 (out_2, in_1[0], in_1[1], in_1[2], in_1[3], in_1[4], in_1[5], in_1[6], in_1[7], in_1[8], in_1[9], in_1[10], in_1[11], in_1[12], in_1[13], in_1[14], in_1[15], in_1[16], in_1[17], in_1[18], in_1[19], in_1[20], in_1[21], in_1[22], in_1[23], in_1[24], in_1[25], in_1[26], in_1[27], in_1[28], in_1[29], in_1[30], in_1[31]);
endmodule

module jr (
  input  [5:0] func,
  input  [5:0] OpCode,
  output izlaz
);

  wire and_1_out, nor_1_out;

  nor nor_1 (nor_1_out, OpCode[0], OpCode[1], OpCode[2], OpCode[3], OpCode[4], OpCode[5]);
  and and_1 (and_1_out, ~func[5], ~func[4], func[3], ~func[2], ~func[1], ~func[0]);  // AND_Gate
  and and_2 (izlaz, and_1_out, nor_1_out);
endmodule

module Ext (
  input  [15:0] Imm,
  input  ext,
  output [31:0] izlaz
);

  and and_1 (izlaz[31], Imm[15], ext);

  assign izlaz[30:0] = {{15{izlaz[31]}}, Imm};
endmodule
